// Logisim project tt_test.circ as structural Verilog: 1 circuit, main circuit main
module main (
  input  RST,
  input  CLK,
  output O_1,
  output O_2,
  output O_3,
  output O_0
);

  wire buffer_1_out, buffer_2_out, buffer_3_out, buffer_4_out;

  D_Flip_Flop d_ff_1 (.D(buffer_4_out), .clk(CLK), .Q(O_0), .preset(RST));  // open: Qn, reset
  buf buffer_1 (buffer_1_out, O_0);
  D_Flip_Flop d_ff_2 (.D(buffer_1_out), .clk(CLK), .Q(O_1), .reset(RST));  // open: Qn, preset
  D_Flip_Flop d_ff_3 (.D(buffer_2_out), .clk(CLK), .Q(O_2), .reset(RST));  // open: Qn, preset
  buf buffer_2 (buffer_2_out, O_1);
  D_Flip_Flop d_ff_4 (.D(buffer_3_out), .clk(CLK), .Q(O_3), .reset(RST));  // open: Qn, preset
  buf buffer_3 (buffer_3_out, O_2);
  buf buffer_4 (buffer_4_out, O_3);
endmodule
